// Logisim project multiplicador binario esquematico.circ as structural Verilog: 1 circuit, main circuit main
module main (
  input  in_1,
  input  in_2,
  input  in_3,
  input  in_4,
  input  in_5,
  input  in_6,
  input  in_7,
  input  in_8,
  input  in_9,
  input  in_10,
  output out_11,
  output out_12,
  output out_13,
  output out_14,
  output out_15,
  output out_16,
  output out_17,
  output out_18,
  output out_19,
  output out_20,
  output out_21,
  output out_22,
  output out_23,
  output out_24,
  output out_25,
  output out_26,
  output out_27
);

  wire and_1_out, and_2_out, and_3_out, and_5_out, and_6_out, nand_1_out, nand_2_out, nand_4_out, nand_5_out,
       not_1_out, not_2_out, not_3_out, not_4_out, not_5_out, not_6_out, not_7_out, not_8_out, not_9_out;
  wire [0:0] and_4_out, multiplexer_3_out, multiplexer_5_out, multiplexer_7_out, nand_3_out;
  wire [1:0] and_8_out, and_9_out, multiplexer_9_out, multiplexer_13_out, nand_6_out;

  Multiplexer #(.select(2)) multiplexer_1 (
    .in0(1'b0), .in1(1'b1), .in2(1'b1), .in3(1'b0), .out(out_22), .sel({out_18, in_10}));  // open: en
  Multiplexer #(.select(2)) multiplexer_2 (
    .in0(1'b0), .in1(1'b0), .in2(1'b0), .in3(1'b1), .sel({out_18, in_10}));  // open: out, en
  nand nand_1 (nand_1_out, in_7, in_1);
  not not_1 (not_1_out, nand_1_out);
  not nand_2 (nand_2_out, in_8);  // NAND_Gate
  and and_1 (and_1_out, in_1, in_9);
  Multiplexer #(.select(2)) multiplexer_3 (
    .in0(nand_1_out), .in1(not_1_out), .in2(not_1_out), .in3(nand_1_out), .out(multiplexer_3_out[0]),
    .sel({out_12, in_6}));  // open: en
  not not_2 (not_2_out, nand_2_out);
  not not_3 (not_3_out, and_1_out);
  nand nand_3 (nand_3_out[0], in_5, in_1);
  Multiplexer #(.select(2)) multiplexer_4 (
    .in0(1'b0), .in1(nand_1_out), .in2(nand_1_out), .in3(1'b1), .out(out_11), .sel({out_12, in_6}));  // open: en
  Multiplexer #(.select(2)) multiplexer_5 (
    .in0(nand_2_out), .in1(not_2_out), .in2(not_2_out), .in3(nand_2_out), .out(multiplexer_5_out[0]),
    .sel({out_15, out_11}));  // open: en
  Multiplexer #(.select(2)) multiplexer_6 (
    .in0(and_1_out), .in1(not_3_out), .in2(not_3_out), .in3(and_1_out), .out(out_23),
    .sel({out_19, multiplexer_7_out[0]}));  // open: en
  Multiplexer #(.select(2)) multiplexer_7 (
    .in0(1'b0), .in1(nand_2_out), .in2(nand_2_out), .in3(1'b1), .out(multiplexer_7_out[0]),
    .sel({out_15, out_11}));  // open: en
  Multiplexer #(.select(2)) multiplexer_8 (
    .in0(1'b0), .in1(and_1_out), .in2(and_1_out), .in3(1'b1), .out(out_18),
    .sel({out_19, multiplexer_7_out[0]}));  // open: en
  and and_2 (and_2_out, in_7, in_2);
  and and_3 (and_3_out, in_8, in_2);
  not not_4 (not_4_out, and_2_out);
  nand nand_4 (nand_4_out, in_9, in_2);
  Multiplexer #(.select(2)) multiplexer_9 (
    .in0(and_2_out), .in1(not_4_out), .in2(not_4_out), .in3(and_2_out), .out(multiplexer_9_out[0]),
    .sel({out_13, nand_3_out[0]}));  // open: en
  Multiplexer #(.select(2)) multiplexer_10 (
    .in0(1'b0), .in1(and_2_out), .in2(and_2_out), .in3(1'b1), .out(out_12), .sel({out_13, nand_3_out[0]}));  // open: en
  not not_5 (not_5_out, nand_4_out);
  not not_6 (not_6_out, and_3_out);
  Multiplexer #(.select(2)) multiplexer_11 (
    .in0(nand_4_out), .in1(not_5_out), .in2(not_5_out), .in3(nand_4_out), .out(out_24),
    .sel({out_17, multiplexer_5_out[0]}));  // open: en
  and and_4 (and_4_out[0], in_5, in_2);
  and and_5 (and_5_out, in_7, in_3);
  Multiplexer #(.select(2)) multiplexer_12 (
    .in0(1'b0), .in1(nand_4_out), .in2(nand_4_out), .in3(1'b1), .out(out_19),
    .sel({out_17, multiplexer_5_out[0]}));  // open: en
  and and_6 (and_6_out, in_3, in_8);
  Multiplexer #(.select(2)) multiplexer_13 (
    .in0(and_3_out), .in1(not_6_out), .in2(not_6_out), .in3(and_3_out), .out(multiplexer_13_out[0]),
    .sel({out_16, multiplexer_3_out[0]}));  // open: en
  nand nand_5 (nand_5_out, in_9, in_3);
  not not_7 (not_7_out, and_5_out);
  Multiplexer #(.select(2)) multiplexer_14 (
    .in0(1'b0), .in1(and_3_out), .in2(and_3_out), .in3(1'b1), .out(out_15),
    .sel({out_16, multiplexer_3_out[0]}));  // open: en
  Multiplexer #(.select(2)) multiplexer_15 (
    .in0(and_5_out), .in1(not_7_out), .in2(not_7_out), .in3(and_5_out), .out(and_9_out[1]),
    .sel({out_14, and_4_out[0]}));  // open: en
  not not_8 (not_8_out, nand_5_out);
  Multiplexer #(.select(2)) multiplexer_16 (
    .in0(1'b0), .in1(and_5_out), .in2(and_5_out), .in3(1'b1), .out(out_13), .sel({out_14, and_4_out[0]}));  // open: en
  not not_9 (not_9_out, and_6_out);
  and and_7 (and_8_out[1], in_5, in_3);
  Multiplexer #(.select(2)) multiplexer_17 (
    .in0(and_6_out), .in1(not_9_out), .in2(not_9_out), .in3(and_6_out), .out(nand_6_out[1]),
    .sel(multiplexer_9_out));  // open: en
  Multiplexer #(.select(2)) multiplexer_18 (
    .in0(nand_5_out), .in1(not_8_out), .in2(not_8_out), .in3(nand_5_out), .out(out_25),
    .sel(multiplexer_13_out));  // open: en
  Multiplexer #(.select(2)) multiplexer_19 (
    .in0(1'b0), .in1(and_6_out), .in2(and_6_out), .in3(1'b1), .out(out_16), .sel(multiplexer_9_out));  // open: en
  Multiplexer #(.select(2)) multiplexer_20 (
    .in0(1'b0), .in1(nand_5_out), .in2(nand_5_out), .in3(1'b1), .out(out_17), .sel(multiplexer_13_out));  // open: en
  and and_8 (and_8_out[0], in_4, in_7);
  and and_9 (and_9_out[0], in_8, in_4);
  nand nand_6 (nand_6_out[0], in_9, in_4);
  Multiplexer #(.select(2)) multiplexer_21 (
    .in0(1'b0), .in1(1'b1), .in2(1'b1), .in3(1'b0), .out(out_20), .sel(and_8_out));  // open: en
  Multiplexer #(.select(2)) multiplexer_22 (
    .in0(1'b0), .in1(1'b1), .in2(1'b1), .in3(1'b0), .out(out_27), .sel(and_9_out));  // open: en
  Multiplexer #(.select(2)) multiplexer_23 (
    .in0(1'b0), .in1(1'b1), .in2(1'b1), .in3(1'b0), .out(out_26), .sel(nand_6_out));  // open: en
  Multiplexer #(.select(2)) multiplexer_24 (
    .in0(1'b0), .in1(1'b0), .in2(1'b0), .in3(1'b1), .out(out_14), .sel(and_8_out));  // open: en
  Multiplexer #(.select(2)) multiplexer_25 (
    .in0(1'b0), .in1(1'b0), .in2(1'b0), .in3(1'b1), .out(multiplexer_9_out[1]), .sel(and_9_out));  // open: en
  Multiplexer #(.select(2)) multiplexer_26 (
    .in0(1'b0), .in1(1'b0), .in2(1'b0), .in3(1'b1), .out(multiplexer_13_out[1]), .sel(nand_6_out));  // open: en
  and and_10 (out_21, in_5, in_4);
endmodule
